# Fritzing sketch electronics (saved by Fritzing 0.9.2b)
breadboards: 1

parts:
  LCD_Display = LCD screen
  ARM_2_Servo = Basic Servo
  ARM_1_Servo = Basic Servo
  GRIPPER_Servo = Basic Servo
  RIGHT_LCD_Key = Pushbutton [package="[THT]"]
  RHT1 = Humidity and Temperature Sensor RHT03
  LEFT_LCD_Key = Pushbutton [package="[THT]"]
  RIGHT_Joystick = Thumb Joystick
  LEFT_Joystick = Thumb Joystick
  Part1 = Arduino Nano (Rev3.0)
  BASE_Servo = Basic Servo
  RTC_DS1302 = RTC_DS1302_module

nets (from the schematic view):
  N1: LCD_Display.RS, Part1.D13/SCK
  N2: LCD_Display.E, Part1.D12/MISO
  N3: LCD_Display.DB4, Part1.D11/MOSI
  N4: LCD_Display.DB5, Part1.D10
  N5: LCD_Display.DB6, Part1.D9
  N6: LCD_Display.DB7, Part1.D8
  N7: ARM_2_Servo.pulse, Part1.D4
  N8: ARM_1_Servo.pulse, Part1.D5
  N9: GRIPPER_Servo.pulse, Part1.D6
  N10: RIGHT_LCD_Key.Pin_1, RIGHT_LCD_Key.Pin_2
  N11: RIGHT_LCD_Key.Pin_3, RIGHT_LCD_Key.Pin_4, Part1.A6
  N12: RHT1.Data-signal, Part1.D0/RX
  N13: LEFT_LCD_Key.Pin_1, LEFT_LCD_Key.Pin_2
  N14: LEFT_LCD_Key.Pin_3, LEFT_LCD_Key.Pin_4, Part1.A7
  N15: RIGHT_Joystick.SEL, Part1.A2
  N16: RIGHT_Joystick.HORZ, Part1.A0
  N17: RIGHT_Joystick.VERT, Part1.A1
  N18: LEFT_Joystick.SEL, Part1.A5
  N19: LEFT_Joystick.HORZ, Part1.A3
  N20: LEFT_Joystick.VERT, Part1.A4
  N21: Part1.D1/TX, RTC_DS1302.RST
  N22: Part1.D2, RTC_DS1302.DAT
  N23: Part1.D3, RTC_DS1302.CLK
  N24: Part1.D7, BASE_Servo.pulse

custom parts:
  RTC_DS1302_module: Arduino module DS1302 SPI Real Time Clock
